// Digital circuit ALU.dig as structural Verilog
module ALU (
  input  [7:0] a,
  input  [7:0] b,
  input  [2:0] opcode,
  output [7:0] out
);

  wire \and , multiplicacao, O_out, \or , or_1_out, shift_left, shift_right, soma, somador_8bits_1_overflow,
       subtracao, subtrator_8bits_1_overflow, \xor ;
  wire [7:0] out_and, out_multi, out_or, out_shift, out_sub, out_sum, out_xor, shift_left_right_1_out;

  shift_left_right shift_left_right_1 (.left_right(shift_left), .in(b), .out(shift_left_right_1_out));
  or or_1 (or_1_out, shift_right, shift_left);
  opcode_and opcode_and_1 (
    .opcode(or_1_out), .S_in(shift_left_right_1_out), .s_0out(out_shift[0]), .s_1out(out_shift[1]),
    .s_2out(out_shift[2]), .s_3out(out_shift[3]), .s_4out(out_shift[4]), .s_5out(out_shift[5]),
    .s_6out(out_shift[6]), .s_7out(out_shift[7]));
  multiplicador_4_4bits multiplicador_4_4bits_1 (.a_in(a), .b_in(b));  // open: out
  and_operator and_operator_1 (.a_in(a), .b_in(b), .opcode(\and ), .out_and(out_and));
  // opcode_and opcode_and_2: pin names not known; wires that end beside it: multiplicacao
  or_operator or_operator_1 (.a_in(a), .b_in(b), .opcode(\or ), .out_and(out_or));
  subtrator_8bits subtrator_8bits_1 (.b_in(b), .a_in(a), .Overflow(subtrator_8bits_1_overflow));  // open: out
  // opcode_and opcode_and_3: pin names not known; wires that end beside it: subtracao
  xor_operator xor_operator_1 (.a_in(a), .b_in(b), .opcode(\xor ), .out_and(out_xor));
  and and_1 (O_out, subtracao, subtrator_8bits_1_overflow);
  somador_8bits somador_8bits_1 (.b_in(b), .a_in(a), .Overflow(somador_8bits_1_overflow));  // open: out
  // opcode_and opcode_and_4: pin names not known; wires that end beside it: soma
  and and_2 (O_out, soma, somador_8bits_1_overflow);
  decoder_opcode decoder_opcode_1 (
    .opcode(opcode), .Soma(soma), .subtrator(subtracao), .multiplicador(multiplicacao),
    .shift_right(shift_right), .shift_left(shift_left), .\and (\and ), .\or (\or ), .\xor (\xor ));
  Multiplexer #(.Selector_Bits(3), .Bits(8)) multiplexer_1 (
    .sel(opcode), .in_0(out_sum), .in_1(out_sub), .in_2(out_multi), .in_3(out_shift), .in_4(out_shift),
    .in_5(out_and), .in_6(out_or), .in_7(out_xor), .out(out));

  // Notes on the sheet:
  //   Operações Legenda:
  //   Soma - 000
  //   Subtração - 001
  //   Multiplicação - 010
  //   Shift_left - 011
  //   shift_right - 100
  //   and - 101
  //   or - 110
  //   xor - 111
endmodule
