// Digital circuit CPU_8bits.dig as structural Verilog
module CPU_8bits (
  input  [2:0] PC
);

  wire Clock_out;
  wire [3:0] register_1_q, register_1_q_2;
  wire [7:0] alu_1_out;
  wire [11:0] eepromdualport_1_d;

  Button Clock (.out(Clock_out));
  EEPROMDualPort #(.AddrBits(3), .Bits(12)) eepromdualport_1 (
    .A(PC), .Din({12{1'b0}}), .str(1'b0), .C(Clock_out), .ld(1'b1), .D(eepromdualport_1_d));
  ALU alu_1 (
    .a(eepromdualport_1_d[7:0]), .b({register_1_q_2, register_1_q}), .opcode(eepromdualport_1_d[10:8]),
    .out(alu_1_out));
  Register #(.Bits(8)) register_1 (.D(alu_1_out), .C(Clock_out), .en(1'b1), .Q({register_1_q_2, register_1_q}));
  Seven_Seg_Hex seven_seg_hex_1 (.d(register_1_q_2), .dp(1'b0));
  Seven_Seg_Hex seven_seg_hex_2 (.d(register_1_q), .dp(1'b0));

  // Notes on the sheet:
  //   Operações no EEFROM
  //   1° soma 2
  //   2° subtrai 2
  //   3° multiplica por 2
  //   4° shift_left
  //   5° shift_right
  //   6° And
  //   7° or
  //   8° xor
  //   contents of eepromdualport_1 (hex, n*v repeats v):
  //   2,202,402,600,800,a05,c06,e07
endmodule
