// Digital circuit Somador 1 bit.dig as structural Verilog
module Somador_1_bit (
  input  Cin,
  input  x,
  input  y,
  output Soma,
  output Cout
);

  wire and_1_out, and_2_out, xor_1_out;

  and and_1 (and_1_out, y, x);
  and and_2 (and_2_out, Cin, xor_1_out);
  or or_1 (Cout, and_2_out, and_1_out);
  xor xor_1 (xor_1_out, y, x);
  xor xor_2 (Soma, Cin, xor_1_out);
endmodule
