// Digital circuit and_operator.dig as structural Verilog
module and_operator (
  input  [7:0] a_in,
  input  [7:0] b_in,
  input  opcode,
  output [7:0] out_and
);

  wire and_1_out, and_2_out, and_3_out, and_4_out, and_5_out, and_6_out, and_7_out, and_8_out;

  and and_1 (and_1_out, b_in[7], a_in[7]);
  and and_2 (and_2_out, b_in[6], a_in[6]);
  and and_3 (and_3_out, b_in[5], a_in[5]);
  and and_4 (and_4_out, b_in[4], a_in[4]);
  and and_5 (and_5_out, b_in[3], a_in[3]);
  and and_6 (and_6_out, b_in[2], a_in[2]);
  and and_7 (and_7_out, b_in[1], a_in[1]);
  and and_8 (and_8_out, b_in[0], a_in[0]);
  // opcode_and opcode_and_1: pin names not known; wires that end beside it: opcode

  // Other names for the same wires on the sheet: a_0 = a_in[0]; a_1 = a_in[1]; a_2 = a_in[2]; a_3 = a_in[3];
  //   a_4 = a_in[4]; a_5 = a_in[5]; a_6 = a_in[6]; a_7 = a_in[7]; b_0 = b_in[0]; b_1 = b_in[1]; b_2 = b_in[2];
  //   b_3 = b_in[3]; b_4 = b_in[4]; b_5 = b_in[5]; b_6 = b_in[6]; b_7 = b_in[7]
endmodule
