// Digital circuit decoder_opcode.dig as structural Verilog
module decoder_opcode (
  input  [2:0] opcode,
  output Soma,
  output subtrator,
  output multiplicador,
  output shift_right,
  output shift_left,
  output \and ,
  output \or ,
  output \xor 
);

  wire not_1_out, not_2_out, not_3_out;

  not not_1 (not_1_out, opcode[2]);
  not not_2 (not_2_out, opcode[1]);
  not not_3 (not_3_out, opcode[0]);
  and and_1 (Soma, not_1_out, not_2_out, not_3_out);
  and and_2 (subtrator, not_1_out, not_2_out, opcode[0]);
  and and_3 (multiplicador, not_1_out, opcode[1], not_3_out);
  and and_4 (shift_right, not_1_out, opcode[1], opcode[0]);
  and and_5 (shift_left, opcode[2], not_2_out, not_3_out);
  and and_6 (\and , opcode[2], not_2_out, opcode[0]);
  and and_7 (\or , opcode[2], opcode[1], not_3_out);
  and and_8 (\xor , opcode[2], opcode[1], opcode[0]);
endmodule
