// Digital circuit meioSomador.dig as structural Verilog
module meioSomador (
  input  a,
  input  b,
  output s,
  output c_out
);

  wire and_1_out, and_2_out, not_1_out, not_2_out;

  not not_1 (not_1_out, b);
  not not_2 (not_2_out, a);
  and and_1 (and_1_out, a, not_1_out);
  and and_2 (and_2_out, b, not_2_out);
  and and_3 (c_out, a, b);
  or or_1 (s, and_1_out, and_2_out);
endmodule
