// Digital circuit multiplicador_4-4bits.dig as structural Verilog
module multiplicador_4_4bits (
  input  [7:0] a_in,
  input  [7:0] b_in,
  output [7:0] out
);

  wire and_1_out, and_2_out, and_3_out, and_4_out, and_5_out, and_6_out, and_7_out, and_8_out, and_9_out,
       and_10_out, and_11_out, and_12_out, and_13_out, and_14_out, and_15_out, meiosomador_1_c_out,
       meiosomador_2_c_out, meiosomador_3_c_out, meiosomador_4_c_out, somador_1_bit_2_cout,
       somador_1_bit_2_soma, somador_1_bit_3_cout, somador_1_bit_4_cout, somador_1_bit_4_soma,
       somador_1_bit_5_cout, somador_1_bit_5_soma, somador_1_bit_6_cout, somador_1_bit_6_soma,
       somador_1_bit_7_cout, somador_1_bit_7_soma, somador_1_bit_8_cout, somador_1_bit_8_soma;

  and and_1 (and_1_out, b_in[3], a_in[3]);
  Somador_1_bit somador_1_bit_1 (
    .Cin(somador_1_bit_3_cout), .x(somador_1_bit_2_cout), .y(and_1_out), .Soma(out[6]), .Cout(out[7]));
  and and_2 (and_2_out, b_in[3], a_in[2]);
  and and_3 (and_3_out, b_in[2], a_in[3]);
  Somador_1_bit somador_1_bit_2 (
    .Cin(somador_1_bit_5_cout), .x(and_3_out), .y(and_2_out), .Soma(somador_1_bit_2_soma),
    .Cout(somador_1_bit_2_cout));
  Somador_1_bit somador_1_bit_3 (
    .Cin(meiosomador_1_c_out), .x(somador_1_bit_4_cout), .y(somador_1_bit_2_soma), .Soma(out[5]),
    .Cout(somador_1_bit_3_cout));
  and and_4 (and_4_out, b_in[3], a_in[1]);
  Somador_1_bit somador_1_bit_4 (
    .Cin(somador_1_bit_6_cout), .x(somador_1_bit_5_soma), .y(and_4_out), .Soma(somador_1_bit_4_soma),
    .Cout(somador_1_bit_4_cout));
  and and_5 (and_5_out, b_in[2], a_in[2]);
  Somador_1_bit somador_1_bit_5 (
    .Cin(somador_1_bit_7_cout), .x(and_6_out), .y(and_5_out), .Soma(somador_1_bit_5_soma),
    .Cout(somador_1_bit_5_cout));
  meioSomador meiosomador_1 (
    .a(somador_1_bit_4_soma), .b(meiosomador_2_c_out), .s(out[4]), .c_out(meiosomador_1_c_out));
  and and_6 (and_6_out, b_in[1], a_in[3]);
  and and_7 (and_7_out, b_in[3], a_in[0]);
  and and_8 (and_8_out, b_in[2], a_in[1]);
  Somador_1_bit somador_1_bit_6 (
    .Cin(meiosomador_3_c_out), .x(and_8_out), .y(somador_1_bit_7_soma), .Soma(somador_1_bit_6_soma),
    .Cout(somador_1_bit_6_cout));
  and and_9 (and_9_out, b_in[1], a_in[2]);
  and and_10 (and_10_out, b_in[0], a_in[3]);
  Somador_1_bit somador_1_bit_7 (
    .Cin(somador_1_bit_8_cout), .x(and_10_out), .y(and_9_out), .Soma(somador_1_bit_7_soma),
    .Cout(somador_1_bit_7_cout));
  meioSomador meiosomador_2 (.a(somador_1_bit_6_soma), .b(and_7_out), .s(out[3]), .c_out(meiosomador_2_c_out));
  and and_11 (and_11_out, b_in[2], a_in[0]);
  and and_12 (and_12_out, b_in[1], a_in[1]);
  meioSomador meiosomador_3 (.a(somador_1_bit_8_soma), .b(and_11_out), .s(out[2]), .c_out(meiosomador_3_c_out));
  Somador_1_bit somador_1_bit_8 (
    .Cin(meiosomador_4_c_out), .x(and_13_out), .y(and_12_out), .Soma(somador_1_bit_8_soma),
    .Cout(somador_1_bit_8_cout));
  and and_13 (and_13_out, b_in[0], a_in[2]);
  and and_14 (and_14_out, b_in[1], a_in[0]);
  meioSomador meiosomador_4 (.a(and_15_out), .b(and_14_out), .s(out[1]), .c_out(meiosomador_4_c_out));
  and and_15 (and_15_out, b_in[0], a_in[1]);
  and and_16 (out[0], b_in[0], a_in[0]);

  // Other names for the same wires on the sheet: a_0 = a_in[0]; a_1 = a_in[1]; a_2 = a_in[2]; a_3 = a_in[3];
  //   b_0 = b_in[0]; b_1 = b_in[1]; b_2 = b_in[2]; b_3 = b_in[3]; S0 = out[0]; S1 = out[1]; S2 = out[2]; S3 = out[3];
  //   S4 = out[4]; S5 = out[5]; S6 = out[6]; S7 = out[7]
endmodule
