// Digital circuit opcode_and-1bit.dig as structural Verilog
module opcode_and_1bit (
  input  opcode,
  input  [7:0] S_in,
  output s_0out
);

  and and_1 (s_0out, opcode, S_in[0]);
  // Pins of 1 and 8 bits meet at S_in
endmodule
