// Digital circuit opcode_and.dig as structural Verilog
module opcode_and (
  input  opcode,
  input  [7:0] S_in,
  output s_0out,
  output s_1out,
  output s_2out,
  output s_3out,
  output s_4out,
  output s_5out,
  output s_6out,
  output s_7out
);

  and and_1 (s_7out, opcode, S_in[7]);
  and and_2 (s_6out, opcode, S_in[6]);
  and and_3 (s_5out, opcode, S_in[5]);
  and and_4 (s_3out, opcode, S_in[3]);
  and and_5 (s_4out, opcode, S_in[4]);
  and and_6 (s_2out, opcode, S_in[2]);
  and and_7 (s_1out, opcode, S_in[1]);
  and and_8 (s_0out, opcode, S_in[0]);
endmodule
