// Digital circuit or_operator.dig as structural Verilog
module or_operator (
  input  [7:0] a_in,
  input  [7:0] b_in,
  input  opcode,
  output [7:0] out_and
);

  wire or_1_out, or_2_out, or_3_out, or_4_out, or_5_out, or_6_out, or_7_out, or_8_out;

  or or_1 (or_1_out, b_in[7], a_in[7]);
  or or_2 (or_2_out, b_in[6], a_in[6]);
  or or_3 (or_3_out, b_in[5], a_in[5]);
  or or_4 (or_4_out, b_in[4], a_in[4]);
  or or_5 (or_5_out, b_in[3], a_in[3]);
  or or_6 (or_6_out, b_in[2], a_in[2]);
  or or_7 (or_7_out, b_in[1], a_in[1]);
  or or_8 (or_8_out, b_in[0], a_in[0]);
  // opcode_and opcode_and_1: pin names not known; wires that end beside it: opcode

  // Other names for the same wires on the sheet: a_0 = a_in[0]; a_1 = a_in[1]; a_2 = a_in[2]; a_3 = a_in[3];
  //   a_4 = a_in[4]; a_5 = a_in[5]; a_6 = a_in[6]; a_7 = a_in[7]; b_0 = b_in[0]; b_1 = b_in[1]; b_2 = b_in[2];
  //   b_3 = b_in[3]; b_4 = b_in[4]; b_5 = b_in[5]; b_6 = b_in[6]; b_7 = b_in[7]
endmodule
