// Digital circuit shift_left-right.dig as structural Verilog
module shift_left_right (
  input  left_right,
  input  [7:0] in,
  output [7:0] out
);

  wire and_1_out, and_3_out, and_4_out, and_5_out, and_6_out, and_7_out, and_8_out, and_9_out, and_10_out,
       and_11_out, and_12_out, and_14_out, not_1_out;

  not not_1 (not_1_out, left_right);
  and and_1 (and_1_out, left_right, in[0]);
  and and_2 (out[0], in[1], not_1_out);
  or or_1 (out[1], and_4_out, and_1_out);
  and and_3 (and_3_out, left_right, in[1]);
  and and_4 (and_4_out, in[2], not_1_out);
  and and_5 (and_5_out, left_right, in[2]);
  or or_2 (out[2], and_6_out, and_3_out);
  and and_6 (and_6_out, in[3], not_1_out);
  and and_7 (and_7_out, left_right, in[3]);
  or or_3 (out[3], and_8_out, and_5_out);
  and and_8 (and_8_out, in[4], not_1_out);
  and and_9 (and_9_out, left_right, in[4]);
  or or_4 (out[4], and_10_out, and_7_out);
  and and_10 (and_10_out, in[5], not_1_out);
  or or_5 (out[5], and_12_out, and_9_out);
  and and_11 (and_11_out, left_right, in[5]);
  and and_12 (and_12_out, in[6], not_1_out);
  and and_13 (out[7], left_right, in[6]);
  or or_6 (out[6], and_14_out, and_11_out);
  and and_14 (and_14_out, in[7], not_1_out);
endmodule
