// Digital circuit somador_4bits.dig as structural Verilog
module somador_4bits (
  input  Cin,
  input  a_3,
  input  a_2,
  input  a_1,
  input  a_0,
  input  b_3,
  input  b_2,
  input  b_1,
  input  b_0,
  output c_out,
  output s_0,
  output s_1,
  output s_2,
  output s_3
);

  wire and_1_out, and_2_out, and_3_out, and_4_out, and_5_out, and_6_out, and_7_out, and_8_out, or_2_out,
       or_3_out, or_4_out, xor_1_out, xor_3_out, xor_5_out, xor_7_out;

  and and_1 (and_1_out, b_3, a_3);
  or or_1 (c_out, and_2_out, and_1_out);
  and and_2 (and_2_out, or_2_out, xor_1_out);
  xor xor_1 (xor_1_out, b_3, a_3);
  xor xor_2 (s_3, or_2_out, xor_1_out);
  and and_3 (and_3_out, b_2, a_2);
  and and_4 (and_4_out, or_3_out, xor_3_out);
  or or_2 (or_2_out, and_4_out, and_3_out);
  xor xor_3 (xor_3_out, b_2, a_2);
  xor xor_4 (s_2, or_3_out, xor_3_out);
  and and_5 (and_5_out, b_1, a_1);
  and and_6 (and_6_out, or_4_out, xor_5_out);
  or or_3 (or_3_out, and_6_out, and_5_out);
  xor xor_5 (xor_5_out, b_1, a_1);
  xor xor_6 (s_1, or_4_out, xor_5_out);
  and and_7 (and_7_out, b_0, a_0);
  or or_4 (or_4_out, and_8_out, and_7_out);
  and and_8 (and_8_out, Cin, xor_7_out);
  xor xor_7 (xor_7_out, b_0, a_0);
  xor xor_8 (s_0, Cin, xor_7_out);
endmodule
