// Digital circuit somador_8bits.dig as structural Verilog
module somador_8bits (
  input  [7:0] b_in,
  input  [7:0] a_in,
  output Overflow,
  output [7:0] out
);

  wire _1__bit_c_o, _2_bit_c_o, _3_bit_c_o, _4_bit_c_o, _5_bit_c_o, _6_bit_c_o, _7_bit_c_o;

  Add _8_bit (.a(a_in[7]), .b(b_in[7]), .c_i(_7_bit_c_o), .s(out[7]), .c_o(Overflow));
  Add _7_bit (.a(a_in[6]), .b(b_in[6]), .c_i(_6_bit_c_o), .s(out[6]), .c_o(_7_bit_c_o));
  Add _6_bit (.a(a_in[5]), .b(b_in[5]), .c_i(_5_bit_c_o), .s(out[5]), .c_o(_6_bit_c_o));
  Add _5_bit (.a(a_in[4]), .b(b_in[4]), .c_i(_4_bit_c_o), .s(out[4]), .c_o(_5_bit_c_o));
  Add _4_bit (.a(a_in[3]), .b(b_in[3]), .c_i(_3_bit_c_o), .s(out[3]), .c_o(_4_bit_c_o));
  Add _3_bit (.a(a_in[2]), .b(b_in[2]), .c_i(_2_bit_c_o), .s(out[2]), .c_o(_3_bit_c_o));
  Add _2_bit (.a(a_in[1]), .b(b_in[1]), .c_i(_1__bit_c_o), .s(out[1]), .c_o(_2_bit_c_o));
  Add _1__bit (.a(a_in[0]), .b(b_in[0]), .c_i(1'b0), .s(out[0]), .c_o(_1__bit_c_o));
endmodule
