// Digital circuit subtrator_8bits.dig as structural Verilog
module subtrator_8bits (
  input  [7:0] b_in,
  input  [7:0] a_in,
  output Overflow,
  output [7:0] out
);

  wire sub_2_c_o, sub_3_c_o, sub_4_c_o, sub_5_c_o, sub_6_c_o, sub_7_c_o, sub_8_c_o;

  Sub sub_1 (.a(a_in[7]), .b(b_in[7]), .c_i(sub_2_c_o), .s(out[7]), .c_o(Overflow));
  Sub sub_2 (.a(a_in[6]), .b(b_in[6]), .c_i(sub_3_c_o), .s(out[6]), .c_o(sub_2_c_o));
  Sub sub_3 (.a(a_in[5]), .b(b_in[5]), .c_i(sub_4_c_o), .s(out[5]), .c_o(sub_3_c_o));
  Sub sub_4 (.a(a_in[4]), .b(b_in[4]), .c_i(sub_5_c_o), .s(out[4]), .c_o(sub_4_c_o));
  Sub sub_5 (.a(a_in[3]), .b(b_in[3]), .c_i(sub_6_c_o), .s(out[3]), .c_o(sub_5_c_o));
  Sub sub_6 (.a(a_in[2]), .b(b_in[2]), .c_i(sub_7_c_o), .s(out[2]), .c_o(sub_6_c_o));
  Sub sub_7 (.a(a_in[1]), .b(b_in[1]), .c_i(sub_8_c_o), .s(out[1]), .c_o(sub_7_c_o));
  Sub sub_8 (.a(a_in[0]), .b(b_in[0]), .c_i(1'b0), .s(out[0]), .c_o(sub_8_c_o));
endmodule
