// Digital circuit xor_operator.dig as structural Verilog
module xor_operator (
  input  [7:0] a_in,
  input  [7:0] b_in,
  input  opcode,
  output [7:0] out_and
);

  wire xor_1_out, xor_2_out, xor_3_out, xor_4_out, xor_5_out, xor_6_out, xor_7_out, xor_8_out;

  xor xor_1 (xor_1_out, b_in[7], a_in[7]);
  xor xor_2 (xor_2_out, b_in[6], a_in[6]);
  xor xor_3 (xor_3_out, b_in[5], a_in[5]);
  xor xor_4 (xor_4_out, b_in[4], a_in[4]);
  xor xor_5 (xor_5_out, b_in[3], a_in[3]);
  xor xor_6 (xor_6_out, b_in[2], a_in[2]);
  xor xor_7 (xor_7_out, b_in[1], a_in[1]);
  xor xor_8 (xor_8_out, b_in[0], a_in[0]);
  // opcode_and opcode_and_1: pin names not known; wires that end beside it: opcode

  // Other names for the same wires on the sheet: a_0 = a_in[0]; a_1 = a_in[1]; a_2 = a_in[2]; a_3 = a_in[3];
  //   a_4 = a_in[4]; a_5 = a_in[5]; a_6 = a_in[6]; a_7 = a_in[7]; b_0 = b_in[0]; b_1 = b_in[1]; b_2 = b_in[2];
  //   b_3 = b_in[3]; b_4 = b_in[4]; b_5 = b_in[5]; b_6 = b_in[6]; b_7 = b_in[7]
endmodule
